# Fritzing sketch hungry hippos - fritzing wiring diagram (saved by Fritzing 1.0.4)
breadboards: 1

parts:
  Part1 = Arduino Nano (Rev3.0)
  J1 = Dagu DGServo 9g header (male) [package=THT]
  J2 = Dagu DGServo 9g header (male) [package=THT]
  J3 = Dagu DGServo 9g header (male) [package=THT]
  J4 = Dagu DGServo 9g header (male) [package=THT]
  J5 = Dagu DGServo 9g header (male) [package=THT]  # not connected
  C2 = Capacitor Polarized [package=cpol-radial-100uf-25v]
  C5 = Capacitor Polarized [package=cpol-radial-100uf-25v]
  C6 = Capacitor Polarized [package=cpol-radial-100uf-25v]  # not connected
  C8 = Electrolytic Capacitor [package="2cm H-Type"]
  C9 = Electrolytic Capacitor [package="2cm H-Type"]  # not connected
  J7 = male pin header, 2 pins [form="♂ (male)"]
  J8 = male pin header, 2 pins [form="♂ (male)"]  # not connected
  J9 = male pin header, 2 pins [form="♂ (male)"]
  J10 = male pin header, 2 pins [form="♂ (male)"]
  J11 = Basic Servo  # not connected

nets:
  N1: Part1.RESET, Part1.D5
  GND: Part1.GND, Part1.A3, Part1.A0, J1.pulse, J2.pulse, J3.gnd, J4.gnd, C2.-, C5.-, C8.+, J7.pin1, J9.pin1, J10.pin1
  N2: Part1.A7, Part1.D13/SCK
  VCC: J1.Vcc, J2.Vcc, J3.Vcc, J4.Vcc, C2.+, C5.+, C8.-, J7.pin2, J9.pin2, J10.pin2

notes:
  470 uF 16V Capacitor
  4700 uF 16V Capacitor
  3-Pin Header for Servo Cable
  to Adaptive Switch Jacks...
  to NeoPixel Strip...
  Main Power Supply (6V)
  to DC screw terminal...
  Legend
  Placeholder for 470 uF capacitor
  Two of the four smaller capacitors
  Servo Connector Presses onto
  the 3-Pin Header
  Adaptive Hungry Hippos Wiring Diagram
  were omitted for clarity
  Servo Pins:  6, 9, 10, 11
  Switch Pins:  A4, A5, A6, A7
  Neopixel Pin:  A0
  Tom Lowell
  tclowell@gmail.com
  April 27, 2025
